// Digital circuit d_flipflop_clr_en.dig as structural Verilog
module d_flipflop_clr_en (
  input  D,
  input  CLK,
  input  CLR,
  input  EN,
  output Q,
  output notQ
);

  wire d_latch_clr_1_q, multiplexer_1_out, not_1_out;

  // Probe on D
  // Probe on CLK
  not not_1 (not_1_out, CLK);
  Multiplexer multiplexer_1 (.sel(EN), .in_0(Q), .in_1(D), .out(multiplexer_1_out));
  d_latch_clr d_latch_clr_1 (.C(not_1_out), .D(multiplexer_1_out), .CLR(CLR), .Q(d_latch_clr_1_q));  // open: notQ
  d_latch_clr d_latch_clr_2 (.C(CLK), .D(d_latch_clr_1_q), .CLR(CLR), .Q(Q), .notQ(notQ));
  // Probe on Q
  // Probe on notQ
endmodule
